// Logisim project TP1 Logisim.circ as structural Verilog: 6 circuits, main circuit main
module additionneur_demi_bit (
  input  x,
  input  y,
  output S,
  output R
);

  xor xor_1 (S, x, y);
  and and_1 (R, x, y);
endmodule

module main (
  input  a,
  input  b,
  output a_b,
  output a_b_2,
  output a_b_3
);

  wire and_3_out, and_4_out, not_1_out;

  not not_1 (not_1_out, a);
  not not_2 (not_1_out, b);
  and and_1 (a_b, a, a, not_1_out);
  and and_2 (a_b_2, not_1_out, b);
  and and_3 (and_3_out, a, b);
  and and_4 (and_4_out, not_1_out, not_1_out);
  or or_1 (a_b_3, and_3_out, and_4_out);
endmodule

module addiotionneur_1BitCOMPLET (
  input  a,
  input  b,
  input  R0,
  output S,
  output R1
);

  wire additionneur_demi_bit_1_r, additionneur_demi_bit_1_s, additionneur_demi_bit_2_r;

  additionneur_demi_bit additionneur_demi_bit_1 (
    .x(a), .y(b), .S(additionneur_demi_bit_1_s), .R(additionneur_demi_bit_1_r));
  additionneur_demi_bit additionneur_demi_bit_2 (
    .x(additionneur_demi_bit_1_s), .y(R0), .S(S), .R(additionneur_demi_bit_2_r));
  or or_1 (R1, additionneur_demi_bit_2_r, additionneur_demi_bit_1_r);
endmodule

module additionneur_4_bits (
  input  [3:0] A,
  input  [3:0] B,
  output [3:0] C,
  output R
);

  wire addiotionneur_1bitcomplet_1_r1, addiotionneur_1bitcomplet_2_r1, addiotionneur_1bitcomplet_3_r1,
       and_1_out, not_1_out;

  not not_1 (not_1_out, A[0]);
  and and_1 (and_1_out, not_1_out, A[0]);
  addiotionneur_1BitCOMPLET addiotionneur_1bitcomplet_1 (
    .a(A[0]), .b(B[0]), .R0(and_1_out), .S(C[0]), .R1(addiotionneur_1bitcomplet_1_r1));
  addiotionneur_1BitCOMPLET addiotionneur_1bitcomplet_2 (
    .a(A[1]), .b(B[1]), .R0(addiotionneur_1bitcomplet_1_r1), .S(C[1]), .R1(addiotionneur_1bitcomplet_2_r1));
  addiotionneur_1BitCOMPLET addiotionneur_1bitcomplet_3 (
    .a(A[2]), .b(B[2]), .R0(addiotionneur_1bitcomplet_2_r1), .S(C[2]), .R1(addiotionneur_1bitcomplet_3_r1));
  addiotionneur_1BitCOMPLET addiotionneur_1bitcomplet_4 (
    .a(A[3]), .b(B[3]), .R0(addiotionneur_1bitcomplet_3_r1), .S(C[3]), .R1(R));
endmodule

module Bascule_RS (
  input  R,
  input  S,
  output out_3
);

  wire nor_2_out;

  nor nor_1 (out_3, R, nor_2_out);
  nor nor_2 (nor_2_out, out_3, S);
endmodule

module COMPTEUR_CYCLIQUE_SUR_4_BITS (
  output a2,
  output a3,
  output a0,
  output a1
);

  wire and_1_out, and_2_out, CLK_out;

  Clock CLK (.out(CLK_out));
  J_K_Flip_Flop j_k_ff_1 (.J(1'b1), .clk(CLK_out), .K(1'b1), .Q(a0));  // open: Qn, preset, en, reset
  J_K_Flip_Flop j_k_ff_2 (.J(a0), .clk(CLK_out), .K(a0), .Q(a1));  // open: Qn, preset, en, reset
  and and_1 (and_1_out, a1, a0);
  J_K_Flip_Flop j_k_ff_3 (.J(and_1_out), .clk(CLK_out), .K(and_1_out), .Q(a2));  // open: Qn, preset, en, reset
  and and_2 (and_2_out, a2, and_1_out);
  J_K_Flip_Flop j_k_ff_4 (.J(and_2_out), .clk(CLK_out), .K(and_2_out), .Q(a3));  // open: Qn, preset, en, reset
endmodule
