// Logisim project TP2 UAL 1 bit , comparateur 4 bits et mini_projet.circ as structural Verilog
module comparateur_4_bits (
  input  [3:0] A,
  input  [3:0] B,
  output A_B,
  output A_B_2,
  output A_B_3
);

  wire and_1_out, and_2_out, and_3_out, comparateur_1bit_1_a_b, comparateur_1bit_1_a_b_3,
       comparateur_1bit_2_a_b, comparateur_1bit_2_a_b_3, comparateur_1bit_3_a_b, comparateur_1bit_3_a_b_3,
       comparateur_1bit_4_a_b, comparateur_1bit_4_a_b_3;

  comparateur_1bit comparateur_1bit_1 (
    .a(A[0]), .b(B[0]), .a_b(comparateur_1bit_1_a_b), .a_b_3(comparateur_1bit_1_a_b_3));  // open: a_b_2
  comparateur_1bit comparateur_1bit_2 (
    .a(A[1]), .b(B[1]), .a_b(comparateur_1bit_2_a_b), .a_b_3(comparateur_1bit_2_a_b_3));  // open: a_b_2
  comparateur_1bit comparateur_1bit_3 (
    .a(A[2]), .b(B[2]), .a_b(comparateur_1bit_3_a_b), .a_b_3(comparateur_1bit_3_a_b_3));  // open: a_b_2
  comparateur_1bit comparateur_1bit_4 (
    .a(A[3]), .b(B[3]), .a_b(comparateur_1bit_4_a_b), .a_b_3(comparateur_1bit_4_a_b_3));  // open: a_b_2
  and and_1 (and_1_out, comparateur_1bit_1_a_b, comparateur_1bit_2_a_b_3, comparateur_1bit_3_a_b_3, comparateur_1bit_4_a_b_3);
  and and_2 (and_2_out, comparateur_1bit_2_a_b, comparateur_1bit_3_a_b_3, comparateur_1bit_4_a_b_3);
  and and_3 (and_3_out, comparateur_1bit_3_a_b, comparateur_1bit_4_a_b_3);
  and and_4 (A_B_3, comparateur_1bit_1_a_b_3, comparateur_1bit_2_a_b_3, comparateur_1bit_3_a_b_3, comparateur_1bit_4_a_b_3);
  or or_1 (A_B, and_1_out, and_2_out, comparateur_1bit_4_a_b, and_3_out);
  nor nor_1 (A_B_2, A_B, A_B_3);
endmodule

module comparateur_1bit (
  input  a,
  input  b,
  output a_b,
  output a_b_2,
  output a_b_3
);

  wire and_3_out, and_4_out, not_1_out, not_2_out;

  not not_1 (not_1_out, a);
  not not_2 (not_2_out, b);
  and and_1 (a_b, a, not_2_out, not_2_out, not_2_out);
  and and_2 (a_b_2, not_1_out, b);
  and and_3 (and_3_out, not_1_out, not_2_out);
  and and_4 (and_4_out, b, a);
  or or_1 (a_b_3, and_3_out, and_4_out);
endmodule

module _1_bit_UAL (
  input  [2:0] Choice,
  input  Sub,
  input  Cin,
  input  A,
  input  B,
  output Result,
  output Cout
);

  wire adder_1_out, and_1_out, nor_1_out, or_1_out, xor_1_out, xor_2_out;

  and and_1 (and_1_out, A, B);
  or or_1 (or_1_out, A, B);
  xor xor_1 (xor_1_out, A, B);
  nor nor_1 (nor_1_out, A, B);
  Adder #(.width(1)) adder_1 (.a(A), .b(xor_2_out), .out(adder_1_out), .cin(Cin), .cout(Cout));
  xor xor_2 (xor_2_out, B, Sub);
  Multiplexer #(.select(3), .enable("false")) multiplexer_1 (
    .in0(and_1_out), .in1(or_1_out), .in2(xor_1_out), .in3(nor_1_out), .in4(adder_1_out), .out(Result),
    .sel(Choice));  // open: in5, in6, in7
endmodule

module _8_bit_UAL (
  input  Cin,
  input  Sub,
  input  [2:0] Choice,
  input  [7:0] in_4,
  input  [7:0] in_5,
  output [7:0] Result
);

  wire n1_bit_ual_1_cout, n1_bit_ual_2_cout, n1_bit_ual_3_cout, n1_bit_ual_4_cout, n1_bit_ual_5_cout,
       n1_bit_ual_6_cout, n1_bit_ual_7_cout;

  _1_bit_UAL u_1_bit_ual_1 (
    .A(in_4[0]), .B(in_5[0]), .Sub(Sub), .Cin(Cin), .Choice(Choice), .Result(Result[0]),
    .Cout(n1_bit_ual_1_cout));
  _1_bit_UAL u_1_bit_ual_2 (
    .A(in_4[1]), .B(in_5[1]), .Sub(Sub), .Cin(n1_bit_ual_1_cout), .Choice(Choice), .Result(Result[1]),
    .Cout(n1_bit_ual_2_cout));
  _1_bit_UAL u_1_bit_ual_3 (
    .A(in_4[2]), .B(in_5[2]), .Sub(Sub), .Cin(n1_bit_ual_2_cout), .Choice(Choice), .Result(Result[2]),
    .Cout(n1_bit_ual_3_cout));
  _1_bit_UAL u_1_bit_ual_4 (
    .A(in_4[3]), .B(in_5[3]), .Sub(Sub), .Cin(n1_bit_ual_3_cout), .Choice(Choice), .Result(Result[3]),
    .Cout(n1_bit_ual_4_cout));
  _1_bit_UAL u_1_bit_ual_5 (
    .A(in_4[4]), .B(in_5[4]), .Sub(Sub), .Cin(n1_bit_ual_4_cout), .Choice(Choice), .Result(Result[4]),
    .Cout(n1_bit_ual_5_cout));
  _1_bit_UAL u_1_bit_ual_6 (
    .A(in_4[5]), .B(in_5[5]), .Sub(Sub), .Cin(n1_bit_ual_5_cout), .Choice(Choice), .Result(Result[5]),
    .Cout(n1_bit_ual_6_cout));
  _1_bit_UAL u_1_bit_ual_7 (
    .A(in_4[6]), .B(in_5[6]), .Sub(Sub), .Cin(n1_bit_ual_6_cout), .Choice(Choice), .Result(Result[6]),
    .Cout(n1_bit_ual_7_cout));
  _1_bit_UAL u_1_bit_ual_8 (
    .A(in_4[7]), .B(in_5[7]), .Sub(Sub), .Cin(n1_bit_ual_7_cout), .Choice(Choice), .Result(Result[7]));  // open: Cout
endmodule

module _8_bit_UAL_V2 (
  input  [1:0] in_1,
  input  Cin,
  input  [7:0] A,
  input  [7:0] B,
  output [7:0] S,
  output D
);

  wire adder_1_cout, or_1_out, subtractor_1_bout;
  wire [7:0] adder_1_out, divider_1_out, multiplier_1_cout, multiplier_1_out, subtractor_1_out;

  Adder adder_1 (.a(A), .b(B), .out(adder_1_out), .cin(Cin), .cout(adder_1_cout));
  Subtractor subtractor_1 (.a(A), .b(B), .out(subtractor_1_out), .bin(Cin), .bout(subtractor_1_bout));
  Multiplier multiplier_1 (.a(A), .b(B), .out(multiplier_1_out), .cout(multiplier_1_cout));  // open: cin
  Divider divider_1 (.a(A), .b(B), .out(divider_1_out));  // open: upper, rem
  Multiplexer #(.select(2), .width(8), .enable("false")) multiplexer_1 (
    .in0(adder_1_out), .in1(subtractor_1_out), .in2(multiplier_1_out), .in3(divider_1_out), .out(S),
    .sel(in_1));
  or or_1 (or_1_out, multiplier_1_cout[0], multiplier_1_cout[1], multiplier_1_cout[2], multiplier_1_cout[3], multiplier_1_cout[4], multiplier_1_cout[5], multiplier_1_cout[6], multiplier_1_cout[7]);
  Multiplexer #(.select(2), .enable("false")) multiplexer_2 (
    .in0(adder_1_cout), .in1(subtractor_1_bout), .in2(or_1_out), .out(D), .sel(in_1));  // open: in3
endmodule
